# Fritzing sketch CDS+LED (saved by Fritzing 0.8.7b)
breadboards: 1

parts:
  부품1 = Arduino Uno (Rev3)
  LED1 = LED - 5mm [color="Red (633nm)" package="5 mm [THT]"]
  LED2 = LED - 5mm [color="Red (633nm)" package="5 mm [THT]"]
  LED3 = LED - 5mm [color="Red (633nm)" package="5 mm [THT]"]
  R3 = Resistor [tolerance=±5% resistance=330 package=THT]
  R4 = Resistor [tolerance=±5% resistance=330 package=THT]
  R5 = Resistor [tolerance=±5% resistance=330 package=THT]
  R6 = Resistor [tolerance=±5% resistance=10k package=THT]
  R7 = Photocell (LDR) [package=THT]

nets:
  N1: 부품1.A1, R6.Pin_0, R7.pin_1
  N2: 부품1.GND, R3.Pin_0, R4.Pin_0, R5.Pin_0, R6.Pin_1
  N3: 부품1.D2, LED1.anode
  N4: 부품1.D4, LED3.anode
  N5: 부품1.5V, LED2.anode, R7.pin_0
  N6: LED1.cathode, LED2.cathode, R5.Pin_1
  N7: LED3.cathode, R4.Pin_1
