# Fritzing sketch CDS (saved by Fritzing 0.8.7b)
breadboards: 1

parts:
  부품1 = Arduino Uno (Rev3)
  R1 = Resistor [tolerance=±5% resistance=330 package=THT]
  R2 = Photocell (LDR) [package=THT]

nets:
  N1: 부품1.A1, 부품1.5V, R2.pin_1
  N2: 부품1.GND, R1.Pin_0
  N3: R1.Pin_1, R2.pin_0
