# Fritzing sketch led234 (saved by Fritzing 0.8.7b)
breadboards: 1

parts:
  부품1 = Arduino Uno (Rev3)
  LED1 = LED - 5mm [color="Red (633nm)" package="5 mm [THT]"]
  LED2 = LED - 5mm [color="Red (633nm)" package="5 mm [THT]"]
  LED3 = LED - 5mm [color="Red (633nm)" package="5 mm [THT]"]
  R3 = Resistor [tolerance=±5% resistance=330 package=THT]
  R4 = Resistor [tolerance=±5% resistance=330 package=THT]
  R5 = Resistor [tolerance=±5% resistance=330 package=THT]

nets:
  N1: 부품1.GND, R3.Pin_0, R4.Pin_0, R5.Pin_0
  N2: 부품1.D2, LED1.anode
  N3: 부품1.D3_PWM, LED2.anode
  N4: LED1.cathode, R5.Pin_1
  N5: LED2.cathode, R3.Pin_1
  N6: LED3.cathode, R4.Pin_1
